# Fritzing sketch LackEnclosureVerkabelung (saved by Fritzing 0.9.2b)
breadboards: 1

parts:
  Arduino = Arduino Nano (Rev3.0)
  Hauptschalter = Toggle Switch [package=THT]
  VentilatorToggle = Pushbutton [package="[THT]"]
  12V_to_5V = NCP1400 Step-Up Breakout
  R1 = Resistor [tolerance=±5% resistance=10k package=THT]
  LED_Beleuchtung = LED - 5mm [color="White (8000K)" package="5 mm [THT]"]

nets:
  GND: Arduino.GND, 12V_to_5V.GND, R1.Pin_0, LED_Beleuchtung.cathode
  N1: Arduino.D9, VentilatorToggle.Pin_3, VentilatorToggle.Pin_4, R1.Pin_1
  N2: Arduino.VIN, VentilatorToggle.Pin_1, VentilatorToggle.Pin_2, 12V_to_5V.VOUT
  12V: Hauptschalter.COM
  N3: Hauptschalter.L2, 12V_to_5V.VIN, LED_Beleuchtung.anode
